# Fritzing sketch PoolWind_interface_board_8wire (saved by Fritzing 1.0.1rc)
circuit board: 11.6604cm x 8.80335cm
perfboards: 2

parts:
  UP-DN = RJ45 Jack [package=rj45-8]
  VoltMeter = INA 260
  U3 = 2-Channel 5v Relay Shield [package=relay-2ch5v10a]  # not connected
  U4 = 2-Channel 5v Relay Shield [package=relay-2ch5v10a]  # not connected
  JP1 = Header 12 [package=1x12_machine-pin-header_lock.004]
  JP2 = Header 12 [package=1x12_machine-pin-header_lock.004]
  JP3 = Header 12 [package=1x12_machine-pin-header_lock.004]
  JP4 = Header 12 [package=1x12_machine-pin-header_lock.004]
  2-24_Raspberry = Header 12 [package=1x12_machine-pin-header_lock.004]
  1-23_Raspberry = Header 12 [package=1x12_machine-pin-header_lock.004]
  R3 = Resistor [tolerance=±5% power=0.25 resistance=220 package=THT]
  R6 = Resistor [tolerance=±5% power=0.25 resistance=220 package=THT]
  Pace_Volt_In = RJ45 Jack [package=rj45-8]

nets:
  N1: UP-DN.1, 2-24_Raspberry.2
  N2: UP-DN.2, JP4.10
  N3: UP-DN.3, JP4.5
  N4: UP-DN.4, JP4.12
  N5: UP-DN.5, JP3.6
  N6: UP-DN.6, JP4.3
  N7: UP-DN.7, JP3.4
  N8: UP-DN.8, VoltMeter.GND, 1-23_Raspberry.5, R3.Pin_0, Pace_Volt_In.3
  N9: VoltMeter.VCC, 1-23_Raspberry.1
  N10: VoltMeter.SCL, 1-23_Raspberry.3
  N11: VoltMeter.SDA, 1-23_Raspberry.2
  N12: VoltMeter.VBUS, Pace_Volt_In.5
  N13: JP1.9, JP2.6, 2-24_Raspberry.10
  N14: JP1.10, 1-23_Raspberry.7
  N15: JP1.12, JP2.9, 2-24_Raspberry.1
  N16: JP2.7, 1-23_Raspberry.6
  N17: JP2.8, 2-24_Raspberry.6
  N18: 2-24_Raspberry.8, R3.Pin_1, R6.Pin_0
  N19: R6.Pin_1, Pace_Volt_In.6

notes:
  remote
  display
  UP
  DN
  ONOFF

custom parts:
  INA 260: Rev. B, add copy
  2-Channel 5v Relay Shield: 2 Channel 5v Relay Shield w. 2x SPD-06VDC-SD-C
